# Fritzing sketch Untitled Sketch 2 (saved by Fritzing 0.9.3b)
breadboards: 1

parts:
  Raspberry_Pi1 = Raspberry Pi 2
  LED2 = smd LED [color="Red (633nm)" package="0805 [SMD]"]
  LED3 = smd LED [color="Red (633nm)" package="0805 [SMD]"]
  LED4 = smd LED [color="Red (633nm)" package="0805 [SMD]"]
  R1 = Resistor [tolerance=±5% resistance=330k package=THT]
  R2 = Resistor [tolerance=±5% resistance=330k package=THT]
  R3 = Resistor [tolerance=±5% resistance=330k package=THT]

nets:
  N1: Raspberry_Pi1.GPIO5, R1.Pin_1
  N2: Raspberry_Pi1.GPIO6, R2.Pin_1
  N3: Raspberry_Pi1.GPIO13, R3.Pin_1
  N4: Raspberry_Pi1.GND, LED2.cathode, LED3.cathode, LED4.cathode
  N5: LED2.anode, R1.Pin_0
  N6: LED3.anode, R2.Pin_0
  N7: LED4.anode, R3.Pin_0
